// Logisim project Circuito do elevador para 3 andares.circ as structural Verilog: 1 circuit, main circuit main
module main (
  input  M,
  input  F1,
  input  F2,
  input  F3,
  output out_5
);

  wire and_1_out, and_2_out, and_3_out, not_1_out, not_2_out, not_3_out, not_4_out, not_5_out, not_6_out,
       not_7_out, or_1_out;

  not not_1 (not_1_out, F1);
  not not_2 (not_2_out, M);
  not not_3 (not_3_out, F2);
  not not_4 (not_4_out, F3);
  not not_5 (not_5_out, not_1_out);
  not not_6 (not_6_out, not_4_out);
  not not_7 (not_7_out, not_3_out);
  and and_1 (and_1_out, not_2_out, not_5_out, not_3_out, not_4_out);
  and and_2 (and_2_out, not_2_out, not_1_out, not_3_out, not_6_out);
  and and_3 (and_3_out, not_2_out, not_1_out, not_7_out, not_4_out);
  or or_1 (or_1_out, and_1_out, and_2_out);
  or or_2 (out_5, or_1_out, and_3_out);

  // Notes on the sheet:
  //   Circuito do elevador para 3 andares
endmodule
