// Logisim project Logisim - Segmento -e- trabalho 2.circ as structural Verilog: 1 circuit, main circuit main
module main (
  input  A,
  input  B,
  input  C,
  input  D
);

  wire and_1_out, not_1_out, not_2_out, or_1_out;

  not not_1 (not_1_out, B);
  not not_2 (not_2_out, D);
  or or_1 (or_1_out, not_1_out, C);
  _7_Segment_Display u_7_segment_display_1 (.e(and_1_out));  // open: g, f, a, b, d, c, dp
  and and_1 (and_1_out, not_2_out, or_1_out);
endmodule
